// Logisim project CPU x8086.circ as structural Verilog: 30 circuits, main circuit reg4
module main (
  input  [7:0] INPR
);

  wire AC_output, alu16_1_ac_15, alu16_1_output_e, and_1_out, clock_1_out, DR_output, maincontroller_1_e_clr,
       maincontroller_1_hlt, maincontroller_1_outr_ld, reg16ir_1_output_i;
  wire [1:0] maincontroller_1_ir_bus_ld, maincontroller_1_m____bus_ld, maincontroller_1_tr_bus_ld;
  wire [2:0] maincontroller_1_dr_bus_inc_ld, maincontroller_1_pc_bus_inc_ld, reg16ir_1_decode_ir;
  wire [3:0] maincontroller_1_ac_bus_inc_clr_ld, maincontroller_1_ar_ld_inc_clr_bus;
  wire [6:0] maincontroller_1_alu;
  wire [7:0] reg8_1_output;
  wire [11:0] reg12_1_output, reg12_2_output, reg16ir_1_bus_ir;
  wire [15:0] controlled_buffer_1_out, ram_1_data, reg16_1_output, reg16_2_output, reg16_3_output, undriven;

  _16OR AC (.AC_INPUT(reg16_2_output), .OUTPUT(AC_output));
  _16OR DR (.AC_INPUT(reg16_1_output), .OUTPUT(DR_output));
  MainController maincontroller_1 (
    .Decode_IR(reg16ir_1_decode_ir), .INPUT_B_i(reg16ir_1_bus_ir), .INPUT_I(reg16ir_1_output_i),
    .E(alu16_1_output_e), .AC(AC_output), .AC15(alu16_1_ac_15), .DR(DR_output), .CLK(and_1_out),
    .HLT(maincontroller_1_hlt), .E_CLR(maincontroller_1_e_clr),
    .PC_BUS_INC_LD(maincontroller_1_pc_bus_inc_ld), .AC_BUS_INC_CLR_LD(maincontroller_1_ac_bus_inc_clr_ld),
    .M____BUS_LD(maincontroller_1_m____bus_ld), .ALU(maincontroller_1_alu),
    .AR_LD_INC_CLR_BUS(maincontroller_1_ar_ld_inc_clr_bus), .DR_BUS_INC_LD(maincontroller_1_dr_bus_inc_ld),
    .IR_BUS_LD(maincontroller_1_ir_bus_ld), .TR_BUS_LD(maincontroller_1_tr_bus_ld),
    .OUTR_LD(maincontroller_1_outr_ld));
  Clock clock_1 (.out(clock_1_out));
  and and_1 (and_1_out, ~maincontroller_1_hlt, clock_1_out);  // AND_Gate
  ALU16 alu16_1 (
    .AC(reg16_2_output), .DR(reg16_1_output), .INPR({{8{1'b0}}, INPR}), .\and (maincontroller_1_alu[0]),
    .add(maincontroller_1_alu[1]), .cma(maincontroller_1_alu[2]), .LD_DR(maincontroller_1_alu[3]),
    .LD_INPR(maincontroller_1_alu[4]), .CIR(maincontroller_1_alu[5]), .CIL(maincontroller_1_alu[6]),
    .AC_15(alu16_1_ac_15), .Output_E(alu16_1_output_e), .CLK(and_1_out), .CLR(maincontroller_1_e_clr));
  RAM #(.addrWidth(12), .dataWidth(16), .bus("separate")) ram_1 (
    .addr(reg12_1_output), .din(controlled_buffer_1_out), .data(ram_1_data),
    .str(maincontroller_1_m____bus_ld[0]), .clk(and_1_out));  // open: sel, ld, clr
  // Probe on reg12_1_output
  reg12 reg12_1 (
    .INPUT(controlled_buffer_1_out[11:0]), .CLK(and_1_out), .LD(maincontroller_1_ar_ld_inc_clr_bus[0]),
    .INC(maincontroller_1_ar_ld_inc_clr_bus[1]), .CLR(maincontroller_1_ar_ld_inc_clr_bus[2]),
    .Output(reg12_1_output));
  // Probe on reg12_2_output
  reg12 reg12_2 (
    .INPUT(controlled_buffer_1_out[11:0]), .CLK(and_1_out), .LD(maincontroller_1_pc_bus_inc_ld[0]),
    .INC(maincontroller_1_pc_bus_inc_ld[1]), .Output(reg12_2_output));  // open: CLR
  reg16 reg16_1 (
    .INPUT(controlled_buffer_1_out), .CLK(and_1_out), .LD(maincontroller_1_dr_bus_inc_ld[0]),
    .INC(maincontroller_1_dr_bus_inc_ld[1]), .OUTPUT(reg16_1_output));  // open: CLR
  // Probe on reg16_2_output
  reg16 reg16_2 (
    .INPUT(undriven), .CLK(and_1_out), .LD(maincontroller_1_ac_bus_inc_clr_ld[0]),
    .INC(maincontroller_1_ac_bus_inc_clr_ld[1]), .CLR(maincontroller_1_ac_bus_inc_clr_ld[2]),
    .OUTPUT(reg16_2_output));
  reg8 reg8_1 (
    .INPUT(controlled_buffer_1_out[7:0]), .CLK(and_1_out), .LD(maincontroller_1_outr_ld),
    .OUTPUT(reg8_1_output));  // open: INC, CLR
  // Probe on reg8_1_output
  // Probe on reg16_3_output
  reg16 reg16_3 (
    .INPUT(controlled_buffer_1_out), .CLK(and_1_out), .LD(maincontroller_1_tr_bus_ld[0]),
    .OUTPUT(reg16_3_output));  // open: INC, CLR
  reg16IR reg16ir_1 (
    .INPUT(controlled_buffer_1_out), .CLK(and_1_out), .LD(maincontroller_1_ir_bus_ld[0]),
    .BUS_IR(reg16ir_1_bus_ir), .Output_I(reg16ir_1_output_i), .Decode_IR(reg16ir_1_decode_ir));
  assign controlled_buffer_1_out = maincontroller_1_ir_bus_ld[1] ? {4'b0000, reg16ir_1_bus_ir} : 16'bz;  // Controlled_Buffer controlled_buffer_1
  assign controlled_buffer_1_out = maincontroller_1_m____bus_ld[1] ? ram_1_data : 16'bz;  // Controlled_Buffer controlled_buffer_2
  assign controlled_buffer_1_out = maincontroller_1_ar_ld_inc_clr_bus[3] ? {4'b0000, reg12_1_output} : 16'bz;  // Controlled_Buffer controlled_buffer_3
  assign controlled_buffer_1_out = maincontroller_1_pc_bus_inc_ld[2] ? {4'b0000, reg12_2_output} : 16'bz;  // Controlled_Buffer controlled_buffer_4
  assign controlled_buffer_1_out = maincontroller_1_dr_bus_inc_ld[2] ? reg16_1_output : 16'bz;  // Controlled_Buffer controlled_buffer_5
  assign controlled_buffer_1_out = maincontroller_1_ac_bus_inc_clr_ld[3] ? reg16_2_output : 16'bz;  // Controlled_Buffer controlled_buffer_6
  assign controlled_buffer_1_out = maincontroller_1_tr_bus_ld[1] ? reg16_3_output : 16'bz;  // Controlled_Buffer controlled_buffer_7

  // Notes on the sheet:
  //   AR
  //   PC
  //   DR
  //   AC
  //   OUTR
  //   TR
  //   IR
endmodule

module reg4 (
  input  INC,
  input  LD,
  input  [3:0] INPUT,
  input  CLR,
  input  CLK,
  output [3:0] OUTPUT
);

  wire and_1_out, and_2_out, and_3_out, and_4_out, and_5_out, and_6_out, and_7_out, and_8_out, and_9_out,
       and_10_out, and_11_out, and_12_out, not_1_out, not_2_out, not_3_out, not_4_out, not_5_out, not_6_out,
       or_1_out, or_2_out, or_3_out, or_4_out, or_5_out, or_6_out, or_7_out, or_8_out;

  and and_1 (and_1_out, INC, not_1_out);
  not not_1 (not_1_out, LD);
  not not_2 (not_2_out, not_1_out);
  not not_3 (not_3_out, INPUT[0]);
  not not_4 (not_4_out, INPUT[1]);
  not not_5 (not_5_out, INPUT[2]);
  not not_6 (not_6_out, INPUT[3]);
  and and_2 (and_2_out, not_2_out, INPUT[0]);
  and and_3 (and_3_out, not_2_out, not_3_out);
  and and_4 (and_4_out, not_2_out, INPUT[1]);
  and and_5 (and_5_out, not_2_out, not_4_out);
  and and_6 (and_6_out, not_2_out, INPUT[2]);
  and and_7 (and_7_out, not_2_out, not_5_out);
  and and_8 (and_8_out, not_2_out, INPUT[3]);
  and and_9 (and_9_out, not_2_out, not_6_out);
  and and_10 (and_10_out, and_1_out, OUTPUT[0]);
  and and_11 (and_11_out, and_1_out, OUTPUT[0], OUTPUT[1]);
  and and_12 (and_12_out, and_1_out, OUTPUT[0], OUTPUT[1], OUTPUT[2]);
  or or_1 (or_1_out, and_2_out, and_1_out);
  or or_2 (or_2_out, and_3_out, and_1_out);
  or or_3 (or_3_out, and_4_out, and_10_out);
  or or_4 (or_4_out, and_10_out, and_5_out);
  or or_5 (or_5_out, and_6_out, and_11_out);
  or or_6 (or_6_out, and_11_out, and_7_out);
  or or_7 (or_7_out, and_8_out, and_12_out);
  or or_8 (or_8_out, and_12_out, and_9_out);
  J_K_Flip_Flop j_k_ff_1 (.J(or_1_out), .clk(CLK), .K(or_2_out), .Q(OUTPUT[0]), .reset(CLR));  // open: Qn, preset, en
  J_K_Flip_Flop j_k_ff_2 (.J(or_3_out), .clk(CLK), .K(or_4_out), .Q(OUTPUT[1]), .reset(CLR));  // open: Qn, preset, en
  J_K_Flip_Flop j_k_ff_3 (.J(or_5_out), .clk(CLK), .K(or_6_out), .Q(OUTPUT[2]), .reset(CLR));  // open: Qn, preset, en
  J_K_Flip_Flop j_k_ff_4 (.J(or_7_out), .clk(CLK), .K(or_8_out), .Q(OUTPUT[3]), .reset(CLR));  // open: Qn, preset, en
endmodule

module reg8 (
  input  [7:0] INPUT,
  input  CLK,
  input  LD,
  input  INC,
  input  CLR,
  output [7:0] OUTPUT
);

  reg4 reg4_1 (.INPUT(INPUT[3:0]), .CLK(CLK), .LD(LD), .INC(INC), .CLR(CLR), .OUTPUT(OUTPUT[3:0]));
  reg4 reg4_2 (.INPUT(INPUT[7:4]), .CLK(CLK), .LD(LD), .INC(INC), .CLR(CLR), .OUTPUT(OUTPUT[7:4]));
endmodule

module reg12 (
  input  [11:0] INPUT,
  input  LD,
  input  INC,
  input  CLR,
  input  CLK,
  output [11:0] Output
);

  reg8 reg8_1 (.INPUT(INPUT[7:0]), .CLK(CLK), .LD(LD), .INC(INC), .CLR(CLR), .OUTPUT(Output[7:0]));
  reg4 reg4_1 (.INPUT(INPUT[11:8]), .CLK(CLK), .LD(LD), .INC(INC), .CLR(CLR), .OUTPUT(Output[11:8]));
endmodule

module reg16 (
  input  [15:0] INPUT,
  input  CLK,
  input  LD,
  input  INC,
  input  CLR,
  output [15:0] OUTPUT
);

  reg8 reg8_1 (.INPUT(INPUT[7:0]), .CLK(CLK), .LD(LD), .INC(INC), .CLR(CLR), .OUTPUT(OUTPUT[7:0]));
  reg8 reg8_2 (.INPUT(INPUT[15:8]), .CLK(CLK), .LD(LD), .INC(INC), .CLR(CLR), .OUTPUT(OUTPUT[15:8]));
endmodule

// IR
module reg16IR (
  input  [15:0] INPUT,
  input  CLK,
  input  LD,
  output [11:0] BUS_IR,
  output Output_I,
  output [2:0] Decode_IR
);

  wire [7:7] reg8_2_output;

  reg8 reg8_1 (.INPUT(INPUT[7:0]), .CLK(CLK), .LD(LD), .OUTPUT(BUS_IR[7:0]));  // open: INC, CLR
  reg8 reg8_2 (
    .INPUT(INPUT[15:8]), .CLK(CLK), .LD(LD), .OUTPUT({reg8_2_output[7], Decode_IR, BUS_IR[11:8]}));  // open: INC, CLR
  J_K_Flip_Flop j_k_ff_1 (.J(1'b1), .clk(reg8_2_output[7]), .K(1'b1), .Q(Output_I));  // open: Qn, preset, en, reset
endmodule

module ALU1 (
  input  INPR,
  input  DR,
  input  AC,
  input  cin,
  input  \and ,
  input  add,
  input  cma,
  input  ld_DR,
  input  ld_INPR,
  input  \cır ,
  input  cil,
  input  i_1,
  input  i_1_2,
  output \output ,
  output cout
);

  wire ADD_out, adder_1_out, and_1_out, AND_2_out, CIL_out, CIR_out, CMA_out, Ld_INPR_out, Ld_NPR_out,
       not_1_out;

  Adder #(.width(1)) adder_1 (.a(AC), .b(DR), .out(adder_1_out), .cin(cin), .cout(cout));
  and and_1 (and_1_out, AC, DR);
  not not_1 (not_1_out, AC);
  and AND_2 (AND_2_out, \and , and_1_out);
  and u_ADD (ADD_out, add, adder_1_out);
  and Ld_NPR (Ld_NPR_out, ld_DR, DR);
  and u_CMA (CMA_out, cma, not_1_out);
  and CIR (CIR_out, \cır , i_1_2);
  and u_CIL (CIL_out, cil, i_1);
  and u_Ld_INPR (Ld_INPR_out, ld_INPR, INPR);
  or or_1 (\output , AND_2_out, ADD_out, Ld_NPR_out, CMA_out, CIR_out, CIL_out, Ld_INPR_out);

  // Notes on the sheet:
  //   1 Bitlik ALU Devresi
endmodule

module ALU4 (
  input  [3:0] AC,
  input  [3:0] DR,
  input  [3:0] INPR,
  input  \and ,
  input  add,
  input  cma,
  input  LD_DR,
  input  LD_INPR,
  input  CIR,
  input  CIL,
  input  CLK,
  input  CLR,
  output [3:0] OUTPUT,
  output out_14
);

  wire alu1_1_cout, alu1_2_cout, alu1_3_cout, alu1_4_cout, e_1_ac_0__ac_i_1, e_1_ac_0__cin, e_1_ac_3__ac_i_1;

  ALU1 alu1_1 (
    .\and (\and ), .add(add), .cma(cma), .ld_DR(LD_DR), .ld_INPR(LD_INPR), .\cır (CIR), .cil(CIL),
    .i_1(e_1_ac_0__ac_i_1), .i_1_2(AC[1]), .INPR(INPR[0]), .DR(DR[0]), .AC(AC[0]), .cin(e_1_ac_0__cin),
    .cout(alu1_1_cout), .\output (OUTPUT[0]));
  ALU1 alu1_2 (
    .\and (\and ), .add(add), .cma(cma), .ld_DR(LD_DR), .ld_INPR(LD_INPR), .\cır (CIR), .cil(CIL),
    .i_1(AC[0]), .i_1_2(AC[2]), .INPR(INPR[1]), .DR(DR[1]), .AC(AC[1]), .cin(alu1_1_cout),
    .cout(alu1_2_cout), .\output (OUTPUT[1]));
  ALU1 alu1_3 (
    .\and (\and ), .add(add), .cma(cma), .ld_DR(LD_DR), .ld_INPR(LD_INPR), .\cır (CIR), .cil(CIL),
    .i_1(AC[1]), .i_1_2(AC[3]), .INPR(INPR[2]), .DR(DR[2]), .AC(AC[2]), .cin(alu1_2_cout),
    .cout(alu1_3_cout), .\output (OUTPUT[2]));
  ALU1 alu1_4 (
    .\and (\and ), .add(add), .cma(cma), .ld_DR(LD_DR), .ld_INPR(LD_INPR), .\cır (CIR), .cil(CIL),
    .i_1(AC[2]), .i_1_2(e_1_ac_3__ac_i_1), .INPR(INPR[3]), .DR(DR[3]), .AC(AC[3]), .cin(alu1_3_cout),
    .cout(alu1_4_cout), .\output (OUTPUT[3]));
  E e_1 (
    .AC_3__count(alu1_4_cout), .AC_3__output(AC[3]), .AC_0_output(AC[0]), .CIL(CIL), .CIR(CIR), .ADD(\and ),
    .CLK(CLK), .CLR(CLR), .output_E(out_14), .AC_0__ac_i_1(e_1_ac_0__ac_i_1),
    .AC_3__ac_i_1(e_1_ac_3__ac_i_1), .AC_0__cin(e_1_ac_0__cin));
endmodule

module ALU16 (
  input  [15:0] AC,
  input  [15:0] DR,
  input  [15:0] INPR,
  input  \and ,
  input  add,
  input  cma,
  input  LD_DR,
  input  LD_INPR,
  input  CIR,
  input  CIL,
  input  CLK,
  input  CLR,
  output AC_15,
  output Output_E
);

  wire alu1_1_cout, alu1_2_cout, alu1_3_cout, alu1_4_cout, alu1_5_cout, alu1_6_cout, alu1_7_cout,
       alu1_8_cout, alu1_9_cout, alu1_10_cout, alu1_11_cout, alu1_12_cout, alu1_13_cout, alu1_14_cout,
       alu1_15_cout, alu1_16_cout, e_1_ac_0__ac_i_1, e_1_ac_0__cin, e_1_ac_3__ac_i_1;

  ALU1 alu1_1 (
    .\and (\and ), .add(add), .cma(cma), .ld_DR(LD_DR), .ld_INPR(LD_INPR), .\cır (CIR), .cil(CIL),
    .i_1(e_1_ac_0__ac_i_1), .i_1_2(AC[1]), .INPR(INPR[0]), .DR(DR[0]), .AC(AC[0]), .cin(e_1_ac_0__cin),
    .cout(alu1_1_cout));  // open: output
  ALU1 alu1_2 (
    .\and (\and ), .add(add), .cma(cma), .ld_DR(LD_DR), .ld_INPR(LD_INPR), .\cır (CIR), .cil(CIL),
    .i_1(AC[0]), .i_1_2(AC[2]), .INPR(INPR[1]), .DR(DR[1]), .AC(AC[1]), .cin(alu1_1_cout), .cout(alu1_2_cout));  // open: output
  ALU1 alu1_3 (
    .\and (\and ), .add(add), .cma(cma), .ld_DR(LD_DR), .ld_INPR(LD_INPR), .\cır (CIR), .cil(CIL),
    .i_1(AC[1]), .i_1_2(AC[3]), .INPR(INPR[2]), .DR(DR[2]), .AC(AC[2]), .cin(alu1_2_cout), .cout(alu1_3_cout));  // open: output
  ALU1 alu1_4 (
    .\and (\and ), .add(add), .cma(cma), .ld_DR(LD_DR), .ld_INPR(LD_INPR), .\cır (CIR), .cil(CIL),
    .i_1(AC[2]), .i_1_2(AC[4]), .INPR(INPR[3]), .DR(DR[3]), .AC(AC[3]), .cin(alu1_3_cout), .cout(alu1_4_cout));  // open: output
  ALU1 alu1_5 (
    .\and (\and ), .add(add), .cma(cma), .ld_DR(LD_DR), .ld_INPR(LD_INPR), .\cır (CIR), .cil(CIL),
    .i_1(AC[3]), .i_1_2(AC[5]), .INPR(INPR[4]), .DR(DR[4]), .AC(AC[4]), .cin(alu1_4_cout), .cout(alu1_5_cout));  // open: output
  ALU1 alu1_6 (
    .\and (\and ), .add(add), .cma(cma), .ld_DR(LD_DR), .ld_INPR(LD_INPR), .\cır (CIR), .cil(CIL),
    .i_1(AC[4]), .i_1_2(AC[6]), .INPR(INPR[5]), .DR(DR[5]), .AC(AC[5]), .cin(alu1_5_cout), .cout(alu1_6_cout));  // open: output
  ALU1 alu1_7 (
    .\and (\and ), .add(add), .cma(cma), .ld_DR(LD_DR), .ld_INPR(LD_INPR), .\cır (CIR), .cil(CIL),
    .i_1(AC[5]), .i_1_2(AC[7]), .INPR(INPR[6]), .DR(DR[6]), .AC(AC[6]), .cin(alu1_6_cout), .cout(alu1_7_cout));  // open: output
  ALU1 alu1_8 (
    .\and (\and ), .add(add), .cma(cma), .ld_DR(LD_DR), .ld_INPR(LD_INPR), .\cır (CIR), .cil(CIL),
    .i_1(AC[6]), .i_1_2(AC[8]), .INPR(INPR[7]), .DR(DR[7]), .AC(AC[7]), .cin(alu1_7_cout), .cout(alu1_8_cout));  // open: output
  ALU1 alu1_9 (
    .\and (\and ), .add(add), .cma(cma), .ld_DR(LD_DR), .ld_INPR(LD_INPR), .\cır (CIR), .cil(CIL),
    .i_1(AC[7]), .i_1_2(AC[9]), .INPR(INPR[8]), .DR(DR[8]), .AC(AC[8]), .cin(alu1_8_cout), .cout(alu1_9_cout));  // open: output
  ALU1 alu1_10 (
    .\and (\and ), .add(add), .cma(cma), .ld_DR(LD_DR), .ld_INPR(LD_INPR), .\cır (CIR), .cil(CIL),
    .i_1(AC[8]), .i_1_2(AC[10]), .INPR(INPR[9]), .DR(DR[9]), .AC(AC[9]), .cin(alu1_9_cout),
    .cout(alu1_10_cout));  // open: output
  ALU1 alu1_11 (
    .\and (\and ), .add(add), .cma(cma), .ld_DR(LD_DR), .ld_INPR(LD_INPR), .\cır (CIR), .cil(CIL),
    .i_1(AC[9]), .i_1_2(AC[11]), .INPR(INPR[10]), .DR(DR[10]), .AC(AC[10]), .cin(alu1_10_cout),
    .cout(alu1_11_cout));  // open: output
  ALU1 alu1_12 (
    .\and (\and ), .add(add), .cma(cma), .ld_DR(LD_DR), .ld_INPR(LD_INPR), .\cır (CIR), .cil(CIL),
    .i_1(AC[10]), .i_1_2(AC[12]), .INPR(INPR[11]), .DR(DR[11]), .AC(AC[11]), .cin(alu1_11_cout),
    .cout(alu1_12_cout));  // open: output
  ALU1 alu1_13 (
    .\and (\and ), .add(add), .cma(cma), .ld_DR(LD_DR), .ld_INPR(LD_INPR), .\cır (CIR), .cil(CIL),
    .i_1(AC[11]), .i_1_2(AC[13]), .INPR(INPR[12]), .DR(DR[12]), .AC(AC[12]), .cin(alu1_12_cout),
    .cout(alu1_13_cout));  // open: output
  ALU1 alu1_14 (
    .\and (\and ), .add(add), .cma(cma), .ld_DR(LD_DR), .ld_INPR(LD_INPR), .\cır (CIR), .cil(CIL),
    .i_1(AC[12]), .i_1_2(AC[14]), .INPR(INPR[13]), .DR(DR[13]), .AC(AC[13]), .cin(alu1_13_cout),
    .cout(alu1_14_cout));  // open: output
  ALU1 alu1_15 (
    .\and (\and ), .add(add), .cma(cma), .ld_DR(LD_DR), .ld_INPR(LD_INPR), .\cır (CIR), .cil(CIL),
    .i_1(AC[13]), .i_1_2(AC[15]), .INPR(INPR[14]), .DR(DR[14]), .AC(AC[14]), .cin(alu1_14_cout),
    .cout(alu1_15_cout));  // open: output
  ALU1 alu1_16 (
    .\and (\and ), .add(add), .cma(cma), .ld_DR(LD_DR), .ld_INPR(LD_INPR), .\cır (CIR), .cil(CIL),
    .i_1(AC[14]), .i_1_2(e_1_ac_3__ac_i_1), .INPR(INPR[15]), .DR(DR[15]), .AC(AC[15]), .cin(alu1_15_cout),
    .cout(alu1_16_cout));  // open: output
  E e_1 (
    .AC_3__count(alu1_16_cout), .AC_3__output(AC[15]), .AC_0_output(AC[0]), .CIL(CIL), .CIR(CIR), .ADD(add),
    .CLK(CLK), .CLR(CLR), .output_E(Output_E), .AC_0__ac_i_1(e_1_ac_0__ac_i_1),
    .AC_3__ac_i_1(e_1_ac_3__ac_i_1), .AC_0__cin(e_1_ac_0__cin));

  assign AC_15 = AC[15];
endmodule

module E (
  input  AC_3__count,
  input  AC_3__output,
  input  AC_0_output,
  input  CIL,
  input  CIR,
  input  ADD,
  input  CLK,
  input  CLR,
  output output_E,
  output AC_0__ac_i_1,
  output AC_3__ac_i_1,
  output AC_0__cin
);

  wire and_1_out, and_2_out, and_3_out, and_4_out, and_5_out, d_ff_1_q, not_1_out, or_1_out, or_2_out;

  or or_1 (or_1_out, AC_3__count, AC_3__output, AC_0_output);
  and and_1 (and_1_out, AC_3__count, ADD);
  and and_2 (and_2_out, AC_0_output, CIR);
  and and_3 (and_3_out, AC_3__output, CIL);
  or or_2 (or_2_out, and_1_out, and_2_out, and_3_out);
  not not_1 (not_1_out, or_2_out);
  D_Flip_Flop d_ff_1 (.clk(CLK), .D(output_E), .Q(d_ff_1_q), .reset(CLR));  // open: Qn, preset, en
  and and_4 (and_4_out, or_2_out, or_1_out);
  J_K_Flip_Flop j_k_ff_1 (.J(and_4_out), .clk(CLK), .K(and_5_out), .Q(output_E), .reset(CLR));  // open: Qn, preset, en
  and and_5 (and_5_out, or_1_out, not_1_out);
  and and_6 (AC_0__ac_i_1, CIL, d_ff_1_q);
  and and_7 (AC_3__ac_i_1, CIR, d_ff_1_q);
  and and_8 (AC_0__cin, ADD, d_ff_1_q);
endmodule

// cont
module counter (
  input  CLK,
  input  SC_CLR,
  output [3:0] \output 
);

  wire and_1_out, register_1_q;

  Counter #(.width(4), .max('hf)) counter_1 (
    .count(1'b1), .Q(\output ), .clk(CLK), .clr(register_1_q));  // open: load, D, carry
  Register #(.width(1)) register_1 (.D(SC_CLR), .Q(register_1_q), .clk(CLK), .clr(and_1_out));  // open: en
  and and_1 (and_1_out, CLK, SC_CLR);
endmodule

// M[ ]
module Count_M (
  input  I,
  input  R,
  input  T1,
  input  T3,
  input  T4,
  input  T6,
  input  D0,
  input  D1,
  input  D2,
  input  D3,
  input  D5,
  input  D6,
  input  D7,
  output M____LD,
  output M____BUS
);

  wire and_1_out, and_2_out, and_3_out, and_4_out, and_5_out, and_6_out, not_1_out, not_2_out, or_1_out,
       or_2_out;

  or or_1 (or_1_out, D3, D5);
  not not_1 (not_1_out, R);
  not not_2 (not_2_out, D7);
  or or_2 (or_2_out, D0, D1, D2, D6);
  and and_1 (and_1_out, R, T1);
  and and_2 (and_2_out, D6, T6);
  and and_3 (and_3_out, T4, or_1_out);
  and and_4 (and_4_out, not_1_out, T1);
  and and_5 (and_5_out, not_2_out, I, T3);
  and and_6 (and_6_out, T4, or_2_out);
  or or_3 (M____LD, and_1_out, and_2_out, and_3_out);
  or or_4 (M____BUS, and_4_out, and_5_out, and_6_out);
endmodule

// AR
module Cont_AR (
  input  I,
  input  R,
  input  T0,
  input  T2,
  input  T3,
  input  T4,
  input  T5,
  input  D4,
  input  D5,
  input  D7,
  output AR_LD,
  output AR_INC,
  output AR_CLR,
  output AR_BUS
);

  wire and_1_out, and_2_out, and_3_out, and_6_out, and_7_out, not_1_out, not_2_out, not_3_out;

  not not_1 (not_1_out, R);
  and and_1 (and_1_out, not_1_out, T0);
  not not_2 (not_2_out, R);
  and and_2 (and_2_out, not_2_out, T2);
  not not_3 (not_3_out, D7);
  and and_3 (and_3_out, not_3_out, I, T3);
  and and_4 (AR_INC, D5, T4);
  and and_5 (AR_CLR, R, T0);
  and and_6 (and_6_out, D4, T4);
  and and_7 (and_7_out, D5, T5);
  or or_1 (AR_LD, and_1_out, and_2_out, and_3_out);
  or or_2 (AR_BUS, and_6_out, and_7_out);
endmodule

// DR
module Cont_DR (
  input  T4,
  input  T5,
  input  T6,
  input  D0,
  input  D1,
  input  D2,
  input  D6,
  output DR_LD,
  output DR_INC,
  output DR_BUS
);

  wire and_1_out, and_2_out, or_1_out;

  or or_1 (or_1_out, D0, D1, D2, D6);
  and and_1 (and_1_out, D2, T5);
  and and_2 (and_2_out, D6, T6);
  and and_3 (DR_LD, or_1_out, T4);
  and and_4 (DR_INC, D6, T5);
  or or_2 (DR_BUS, and_1_out, and_2_out);
endmodule

// IR
module Cont_IR (
  input  R,
  input  T1,
  input  T2,
  output IR_LD,
  output IR_BUS
);

  wire not_1_out;

  not not_1 (not_1_out, R);
  and and_1 (IR_LD, not_1_out, T1);
  and and_2 (IR_BUS, not_1_out, T2);
endmodule

// OutR
module Cont_OutR (
  input  p,
  input  B10,
  output OutR_LD
);

  and and_1 (OutR_LD, B10, p);
endmodule

// TR
module Cont_TR (
  input  R,
  input  T0,
  input  T1,
  output TR_LD,
  output TR_BUS
);

  and and_1 (TR_LD, R, T0);
  and and_2 (TR_BUS, R, T1);
endmodule

// PC
module Cont_PC (
  input  E,
  input  AC,
  input  AC_15,
  input  DR,
  input  FGO,
  input  FGI,
  input  p,
  input  r,
  input  R_2,
  input  T0,
  input  T1,
  input  T2,
  input  T4,
  input  T5,
  input  T6,
  input  D4,
  input  D5,
  input  D6,
  input  B1,
  input  B2,
  input  B3,
  input  B4,
  input  B8,
  input  B9,
  output PC_LD,
  output PC_INC,
  output PC_BUS
);

  wire and_1_out, and_2_out, and_3_out, and_4_out, and_5_out, and_6_out, and_7_out, and_8_out, and_9_out,
       and_10_out, and_11_out, and_12_out, and_13_out, and_14_out, and_15_out, and_16_out, and_17_out,
       and_18_out, and_19_out, and_20_out, and_21_out, not_1_out, not_2_out;

  not not_1 (not_1_out, R_2);
  and and_1 (and_1_out, D6, T6);
  and and_2 (and_2_out, r, B4);
  and and_3 (and_3_out, r, B3);
  and and_4 (and_4_out, r, B2);
  and and_5 (and_5_out, r, B1);
  and and_6 (and_6_out, p, B9);
  and and_7 (and_7_out, p, B8);
  not not_2 (not_2_out, R_2);
  and and_8 (and_8_out, D4, T4);
  and and_9 (and_9_out, D5, T5);
  and and_10 (and_10_out, not_1_out, T1);
  and and_11 (and_11_out, R_2, T2);
  and and_12 (and_12_out, and_1_out, ~DR);  // AND_Gate
  and and_13 (and_13_out, and_2_out, ~AC_15);  // AND_Gate
  and and_14 (and_14_out, and_3_out, AC_15);
  and and_15 (and_15_out, and_4_out, ~AC);  // AND_Gate
  and and_16 (and_16_out, and_5_out, ~E);  // AND_Gate
  and and_17 (and_17_out, and_6_out, FGI);
  and and_18 (and_18_out, and_7_out, FGO);
  and and_19 (and_19_out, not_2_out, T0);
  and and_20 (and_20_out, R_2, T0);
  and and_21 (and_21_out, D5, T4);
  or or_1 (PC_LD, and_8_out, and_9_out);
  or or_2 (PC_INC, and_10_out, and_11_out, and_12_out, and_13_out, and_14_out, and_15_out, and_16_out, and_17_out, and_18_out);
  or or_3 (PC_BUS, and_19_out, and_20_out, and_21_out);
endmodule

// AC
module Count_Ac (
  input  B5,
  input  B6,
  input  B7,
  input  B9,
  input  B10,
  input  B11,
  input  p,
  input  r,
  input  T4,
  input  T5,
  input  D0,
  input  D1,
  input  D2,
  input  D3,
  output AC_LD,
  output AC_INC,
  output AC_CLR,
  output AC_BUS
);

  wire and_1_out, and_2_out, and_3_out, and_4_out, and_5_out, or_1_out, or_2_out;

  or or_1 (or_1_out, D0, D1, D2);
  or or_2 (or_2_out, B9, B7, B6);
  and and_1 (and_1_out, or_1_out, T5);
  and and_2 (and_2_out, p, B11);
  and and_3 (and_3_out, D3, T4);
  and and_4 (and_4_out, r, or_2_out);
  and and_5 (and_5_out, p, B10);
  or or_3 (AC_LD, and_1_out, and_2_out);
  and and_6 (AC_INC, r, B5);
  and and_7 (AC_CLR, r, B11);
  or or_4 (AC_BUS, and_3_out, and_4_out, and_5_out);
endmodule

module Cont_Alu (
  input  B6,
  input  B7,
  input  B9,
  input  B11,
  input  p,
  input  r,
  input  T5,
  input  D0,
  input  D1,
  input  D2,
  output AND,
  output ADD,
  output CMA,
  output LD_DR,
  output LD_INPR,
  output CIR,
  output CIL
);

  and and_1 (AND, D0, T5);
  and and_2 (ADD, D1, T5);
  and and_3 (CMA, r, B9);
  and and_4 (LD_DR, T5, D2);
  and and_5 (LD_INPR, p, B11);
  and and_6 (CIR, r, B7);
  and and_7 (CIL, r, B6);
endmodule

module SC_CLR (
  input  p,
  input  r,
  input  R_2,
  input  T2,
  input  T3,
  input  T4,
  input  T5,
  input  T6,
  input  D0,
  input  D1,
  input  D2,
  input  D3,
  input  D4,
  input  D5,
  input  D6,
  input  D7,
  output SC_CLR
);

  wire and_1_out, and_2_out, and_3_out, and_4_out, and_5_out, or_1_out, or_2_out;

  or or_1 (or_1_out, D0, D1, D2);
  or or_2 (or_2_out, D3, D4);
  and and_1 (and_1_out, R_2, T2);
  and and_2 (and_2_out, T5, or_1_out);
  and and_3 (and_3_out, T4, or_2_out);
  and and_4 (and_4_out, D5, T5);
  and and_5 (and_5_out, D6, T6);
  or or_3 (SC_CLR, and_1_out, and_2_out, and_3_out, and_4_out, and_5_out, r, p);
endmodule

module RegisterControl (
  input  I,
  input  E,
  input  AC,
  input  AC15,
  input  DR,
  input  FGO,
  input  FGI,
  input  p,
  input  r,
  input  T0,
  input  T1,
  input  T2,
  input  T3,
  input  T4,
  input  T5,
  input  T6,
  input  D0,
  input  D1,
  input  D2,
  input  D3,
  input  D4,
  input  D5,
  input  D6,
  input  D7,
  input  B0,
  input  B1,
  input  B2,
  input  B3,
  input  B4,
  input  B5,
  input  B6,
  input  B7,
  input  B8,
  input  B9,
  input  B10,
  input  B11,
  output PC_LD,
  output PC_INC,
  output PC_BUS,
  output AC_LD,
  output AC_INC,
  output AC_CLR,
  output AC_BUS,
  output M___LD,
  output M___BUS,
  output AR_LD,
  output AR_INC,
  output AR_CLR,
  output AR_BUS,
  output DR_LD,
  output DR_INC,
  output DR_BUS,
  output R_OUT,
  output IR_LD,
  output IR_BUS,
  output TR_LD,
  output TR_BUS,
  output OUTR_LD,
  output S_OUT,
  output IEN_OUT,
  output FGI_OUT,
  output FGO_OUT
);

  Cont_DR cont_dr_1 (
    .T4(T4), .T5(T5), .T6(T6), .D0(D0), .D1(D1), .D2(D2), .D6(D6), .DR_LD(DR_LD), .DR_INC(DR_INC),
    .DR_BUS(DR_BUS));
  R r_1 (.T0(T0), .T1(T1), .T2(T2), .IEN(IEN_OUT), .FGI(FGI_OUT), .FGO(FGO_OUT), .Output_R(R_OUT));
  Cont_IR cont_ir_1 (.R(R_OUT), .T1(T1), .T2(T2), .IR_LD(IR_LD), .IR_BUS(IR_BUS));
  Cont_TR cont_tr_1 (.R(R_OUT), .T0(T0), .T1(T1), .TR_LD(TR_LD), .TR_BUS(TR_BUS));
  Cont_OutR cont_outr_1 (.p(p), .B10(B10), .OutR_LD(OUTR_LD));
  S s_1 (.B0(B0), .r(r), .Output_S(S_OUT));
  IEN ien_1 (.B6(B6), .p(p), .T2(T2), .R(R_OUT), .B7(B7), .p_2(p), .OUTPUT_IEN(IEN_OUT));
  FGI fgi_1 (.B11(B11), .p(p), .Output_FGI(FGI_OUT));
  FGO fgo_1 (.B8(B8), .p(p), .Output_FGO(FGO_OUT));
  Count_Ac count_ac_1 (
    .B5(B5), .B6(B6), .B7(B7), .B9(B9), .B10(B10), .B11(B11), .p(p), .r(r), .T4(T4), .T5(T5), .D0(D0),
    .D1(D1), .D2(D2), .D3(D3), .AC_LD(AC_LD), .AC_INC(AC_INC), .AC_CLR(AC_CLR), .AC_BUS(AC_BUS));
  Count_M count_m_1 (
    .I(I), .R(R_OUT), .T1(T1), .T3(T3), .T4(T4), .T6(T6), .D0(D0), .D1(D1), .D2(D2), .D3(D3), .D5(D5),
    .D6(D6), .D7(D7), .M____LD(M___LD), .M____BUS(M___BUS));
  Cont_AR cont_ar_1 (
    .I(I), .R(R_OUT), .T0(T0), .T2(T2), .T3(T3), .T4(T4), .T5(T5), .D4(D4), .D5(D5), .D7(D7), .AR_LD(AR_LD),
    .AR_INC(AR_INC), .AR_CLR(AR_CLR), .AR_BUS(AR_BUS));
  Cont_PC cont_pc_1 (
    .E(E), .AC(AC), .AC_15(AC15), .DR(DR), .FGO(FGO), .FGI(FGI), .p(p), .r(r), .R_2(R_OUT), .T0(T0), .T1(T1),
    .T2(T2), .T4(T4), .T5(T5), .T6(T6), .D4(D4), .D5(D5), .D6(D6), .B1(B1), .B2(B2), .B3(B3), .B4(B4),
    .B8(B8), .B9(B9), .PC_LD(PC_LD), .PC_INC(PC_INC), .PC_BUS(PC_BUS));
endmodule

// MainCont
module MainController (
  input  [2:0] Decode_IR,
  input  [11:0] INPUT_B_i,
  input  INPUT_I,
  input  E,
  input  AC,
  input  AC15,
  input  DR,
  input  CLK,
  output [2:0] PC_BUS_INC_LD,
  output [3:0] AC_BUS_INC_CLR_LD,
  output [1:0] M____BUS_LD,
  output [6:0] ALU,
  output [3:0] AR_LD_INC_CLR_BUS,
  output [2:0] DR_BUS_INC_LD,
  output [1:0] IR_BUS_LD,
  output [1:0] TR_BUS_LD,
  output OUTR_LD,
  output HLT,
  output E_CLR
);

  wire r_p_1_p, r_p_1_r, registercontrol_1_fgi_out, registercontrol_1_fgo_out, registercontrol_1_r_out,
       sc_clr_1_sc_clr;
  wire [3:0] counter_1_output;
  wire [4:0] decoder_2_out6;
  wire [6:5] decoder_2_out1;
  wire [7:0] decoder_1_out7;

  r_p r_p_1 (.D7(decoder_1_out7[0]), .I(INPUT_I), .T3(decoder_2_out6[3]), .r(r_p_1_r), .p(r_p_1_p));
  SC_CLR sc_clr_1 (
    .p(r_p_1_p), .r(r_p_1_r), .R_2(registercontrol_1_r_out), .T2(decoder_2_out6[4]), .T3(decoder_2_out6[3]),
    .T4(decoder_2_out6[2]), .T5(decoder_2_out6[1]), .T6(decoder_2_out6[0]), .D0(decoder_1_out7[7]),
    .D1(decoder_1_out7[6]), .D2(decoder_1_out7[5]), .D3(decoder_1_out7[4]), .D4(decoder_1_out7[3]),
    .D5(decoder_1_out7[2]), .D6(decoder_1_out7[1]), .D7(decoder_1_out7[0]), .SC_CLR(sc_clr_1_sc_clr));
  Decoder #(.select(3)) decoder_1 (
    .out0(decoder_1_out7[7]), .out1(decoder_1_out7[6]), .out2(decoder_1_out7[5]), .out3(decoder_1_out7[4]),
    .out4(decoder_1_out7[3]), .out5(decoder_1_out7[2]), .out6(decoder_1_out7[1]), .out7(decoder_1_out7[0]),
    .sel(Decode_IR));  // open: en
  Decoder #(.select(4)) decoder_2 (
    .out0(decoder_2_out1[6]), .out1(decoder_2_out1[5]), .out2(decoder_2_out6[4]), .out3(decoder_2_out6[3]),
    .out4(decoder_2_out6[2]), .out5(decoder_2_out6[1]), .out6(decoder_2_out6[0]), .sel(counter_1_output));  // open: out7, out8, out9, out10, out11, out12, out13, out14, out15, en
  counter counter_1 (.CLK(CLK), .SC_CLR(sc_clr_1_sc_clr), .\output (counter_1_output));
  and and_1 (E_CLR, r_p_1_r, INPUT_B_i[10]);
  Cont_Alu cont_alu_1 (
    .B6(INPUT_B_i[6]), .B7(INPUT_B_i[7]), .B9(INPUT_B_i[9]), .B11(INPUT_B_i[11]), .p(r_p_1_p), .r(r_p_1_r),
    .T5(decoder_2_out6[1]), .D0(decoder_1_out7[7]), .D1(decoder_1_out7[6]), .D2(decoder_1_out7[5]),
    .AND(ALU[0]), .ADD(ALU[1]), .CMA(ALU[2]), .LD_DR(ALU[3]), .LD_INPR(ALU[4]), .CIR(ALU[5]), .CIL(ALU[6]));
  RegisterControl registercontrol_1 (
    .I(INPUT_I), .E(E), .AC(AC), .AC15(AC15), .DR(DR), .FGO(registercontrol_1_fgo_out),
    .FGI(registercontrol_1_fgi_out), .p(r_p_1_p), .r(r_p_1_r), .T0(decoder_2_out1[6]),
    .T1(decoder_2_out1[5]), .T2(decoder_2_out6[4]), .T3(decoder_2_out6[3]), .T4(decoder_2_out6[2]),
    .T5(decoder_2_out6[1]), .T6(decoder_2_out6[0]), .D0(decoder_1_out7[7]), .D1(decoder_1_out7[6]),
    .D2(decoder_1_out7[5]), .D3(decoder_1_out7[4]), .D4(decoder_1_out7[3]), .D5(decoder_1_out7[2]),
    .D6(decoder_1_out7[1]), .D7(decoder_1_out7[0]), .B0(INPUT_B_i[0]), .B1(INPUT_B_i[1]), .B2(INPUT_B_i[2]),
    .B3(INPUT_B_i[3]), .B4(INPUT_B_i[4]), .B5(INPUT_B_i[5]), .B6(INPUT_B_i[6]), .B7(INPUT_B_i[7]),
    .B8(INPUT_B_i[8]), .B9(INPUT_B_i[9]), .B10(INPUT_B_i[10]), .B11(INPUT_B_i[11]), .PC_LD(PC_BUS_INC_LD[0]),
    .PC_INC(PC_BUS_INC_LD[1]), .PC_BUS(PC_BUS_INC_LD[2]), .AC_LD(AC_BUS_INC_CLR_LD[0]),
    .AC_INC(AC_BUS_INC_CLR_LD[1]), .AC_CLR(AC_BUS_INC_CLR_LD[2]), .AC_BUS(AC_BUS_INC_CLR_LD[3]),
    .M___LD(M____BUS_LD[0]), .M___BUS(M____BUS_LD[1]), .AR_LD(AR_LD_INC_CLR_BUS[0]),
    .AR_INC(AR_LD_INC_CLR_BUS[1]), .AR_CLR(AR_LD_INC_CLR_BUS[2]), .AR_BUS(AR_LD_INC_CLR_BUS[3]),
    .DR_LD(DR_BUS_INC_LD[0]), .DR_INC(DR_BUS_INC_LD[1]), .DR_BUS(DR_BUS_INC_LD[2]),
    .R_OUT(registercontrol_1_r_out), .IR_LD(IR_BUS_LD[0]), .IR_BUS(IR_BUS_LD[1]), .TR_LD(TR_BUS_LD[0]),
    .TR_BUS(TR_BUS_LD[1]), .OUTR_LD(OUTR_LD), .S_OUT(HLT), .FGI_OUT(registercontrol_1_fgi_out),
    .FGO_OUT(registercontrol_1_fgo_out));  // open: IEN_OUT

  // Notes on the sheet:
  //   D Decode
  //   T Decode
endmodule

module r_p (
  input  D7,
  input  I,
  input  T3,
  output r,
  output p
);

  wire not_1_out;

  not not_1 (not_1_out, I);
  and and_1 (r, T3, not_1_out, D7);
  and and_2 (p, T3, I, D7);
endmodule

module _16OR (
  input  [15:0] AC_INPUT,
  output OUTPUT
);

  or or_1 (OUTPUT, AC_INPUT[0], AC_INPUT[1], AC_INPUT[2], AC_INPUT[3], AC_INPUT[4], AC_INPUT[5], AC_INPUT[6], AC_INPUT[7], AC_INPUT[8], AC_INPUT[9], AC_INPUT[10], AC_INPUT[11], AC_INPUT[12], AC_INPUT[13], AC_INPUT[14], AC_INPUT[15]);
endmodule

module S (
  input  B0,
  input  r,
  output Output_S
);

  wire and_1_out, undriven;

  and and_1 (and_1_out, r, B0);
  J_K_Flip_Flop j_k_ff_1 (.J(and_1_out), .clk(undriven), .K(and_1_out), .Q(Output_S));  // open: Qn, preset, en, reset
endmodule

module R (
  input  T0,
  input  T1,
  input  T2,
  input  IEN,
  input  FGI,
  input  FGO,
  output Output_R
);

  wire and_1_out, and_2_out, or_1_out;

  or or_1 (or_1_out, FGO, FGI);
  and and_1 (and_1_out, or_1_out, IEN, T2, T1, T0);
  and and_2 (and_2_out, T2, Output_R);
  J_K_Flip_Flop j_k_ff_1 (.J(and_1_out), .K(and_2_out), .Q(Output_R));  // open: clk, Qn, preset, en, reset
endmodule

module IEN (
  input  B6,
  input  p,
  input  T2,
  input  R,
  input  B7,
  input  p_2,
  output OUTPUT_IEN
);

  wire and_1_out, and_2_out, and_3_out, or_1_out;

  and and_1 (and_1_out, p_2, B7);
  and and_2 (and_2_out, R, T2);
  and and_3 (and_3_out, p, B6);
  or or_1 (or_1_out, and_2_out, and_3_out);
  J_K_Flip_Flop j_k_ff_1 (.J(and_1_out), .K(or_1_out), .Q(OUTPUT_IEN));  // open: clk, Qn, preset, en, reset
endmodule

module FGI (
  input  B11,
  input  p,
  output Output_FGI
);

  wire and_1_out;

  and and_1 (and_1_out, p, B11);
  J_K_Flip_Flop j_k_ff_1 (.J(and_1_out), .K(and_1_out), .Q(Output_FGI));  // open: clk, Qn, preset, en, reset
endmodule

module FGO (
  input  B8,
  input  p,
  output Output_FGO
);

  wire and_1_out;

  and and_1 (and_1_out, p, B8);
  J_K_Flip_Flop j_k_ff_1 (.J(and_1_out), .K(and_1_out), .Q(Output_FGO));  // open: clk, Qn, preset, en, reset
endmodule
