// Logisim project CPU.circ as structural Verilog: 19 circuits, main circuit reg4
module main (
  input  [3:0] INPR,
  output E
);

  wire and_1_out, clock_1_out, maincontroller_1_dr_ld, maincontroller_1_e_clr, maincontroller_1_hlt,
       maincontroller_1_outr_ld, reg4_5_p4;
  wire [1:0] maincontroller_1_ir_bus_ld, maincontroller_1_m_____bus_ld;
  wire [2:0] maincontroller_1_ar__bus_inc_ld, maincontroller_1_pc__bus_inc_ld;
  wire [3:0] alu4_1_output, controlled_buffer_1_out, maincontroller_1_ac_bus_clr_inc_ld, reg4_1_output,
       reg4_2_output, reg4_3_output, reg4_4_output, reg4_5_p1, reg8_1_decode_ir, reg8_1_ir;
  wire [6:0] maincontroller_1_alu;
  wire [7:0] ram_1_data;

  MainController maincontroller_1 (
    .IR_4__7(reg8_1_decode_ir), .CLK(and_1_out), .HLT(maincontroller_1_hlt), .E_CLR(maincontroller_1_e_clr),
    .M_____BUS_LD(maincontroller_1_m_____bus_ld), .AR__BUS_INC_LD(maincontroller_1_ar__bus_inc_ld),
    .PC__BUS_INC_LD(maincontroller_1_pc__bus_inc_ld), .DR_LD(maincontroller_1_dr_ld),
    .AC_BUS_CLR_INC_LD(maincontroller_1_ac_bus_clr_inc_ld), .Outr_LD(maincontroller_1_outr_ld),
    .IR_BUS_LD(maincontroller_1_ir_bus_ld), .ALU(maincontroller_1_alu));
  Clock clock_1 (.out(clock_1_out));
  and and_1 (and_1_out, ~maincontroller_1_hlt, clock_1_out);  // AND_Gate
  ALU4 alu4_1 (
    .AC(reg4_4_output), .DR(reg4_3_output), .INPR(INPR), .\and (maincontroller_1_alu[0]),
    .add(maincontroller_1_alu[1]), .cma(maincontroller_1_alu[2]), .LD_DR(maincontroller_1_alu[3]),
    .LD_INPR(maincontroller_1_alu[4]), .CIR(maincontroller_1_alu[5]), .CIL(maincontroller_1_alu[6]),
    .out_14(E), .CLK(and_1_out), .CLR(maincontroller_1_e_clr), .OUTPUT(alu4_1_output));
  RAM #(.addrWidth(4), .bus("separate")) ram_1 (
    .addr(reg4_1_output), .din({controlled_buffer_1_out, reg4_5_p1}), .data(ram_1_data),
    .str(maincontroller_1_m_____bus_ld[0]), .clk(and_1_out));  // open: sel, ld, clr
  // Probe on reg4_1_output
  reg4 reg4_1 (
    .INPUT(reg4_5_p1), .CLK(and_1_out), .LD(maincontroller_1_ar__bus_inc_ld[0]),
    .INC(maincontroller_1_ar__bus_inc_ld[1]), .OUTPUT(reg4_1_output));  // open: CLR
  // Probe on reg4_2_output
  reg4 reg4_2 (
    .INPUT(reg4_5_p1), .CLK(and_1_out), .LD(maincontroller_1_pc__bus_inc_ld[0]),
    .INC(maincontroller_1_pc__bus_inc_ld[1]), .OUTPUT(reg4_2_output));  // open: CLR
  reg4 reg4_3 (
    .INPUT(reg4_5_p1), .CLK(and_1_out), .LD(maincontroller_1_dr_ld), .OUTPUT(reg4_3_output));  // open: INC, CLR
  // Probe on reg4_4_output
  reg4 reg4_4 (
    .INPUT(alu4_1_output), .CLK(and_1_out), .LD(maincontroller_1_ac_bus_clr_inc_ld[0]),
    .INC(maincontroller_1_ac_bus_clr_inc_ld[1]), .CLR(maincontroller_1_ac_bus_clr_inc_ld[2]),
    .OUTPUT(reg4_4_output));
  // Probe on reg4_5_p4
  // reg4 reg4_5: pin names not known; wires that end beside it: reg4_5_p1, and_1_out, maincontroller_1_outr_ld, reg4_5_p4
  // Probe on reg8_1_decode_ir
  reg8 reg8_1 (
    .INPUT({controlled_buffer_1_out, reg4_5_p1}), .CLK(and_1_out), .LD(maincontroller_1_ir_bus_ld[0]),
    .IR(reg8_1_ir), .Decode_IR(reg8_1_decode_ir));
  // Probe on reg8_1_ir
  assign {controlled_buffer_1_out, reg4_5_p1} = maincontroller_1_m_____bus_ld[1] ? ram_1_data : 8'bz;  // Controlled_Buffer controlled_buffer_1
  assign {controlled_buffer_1_out, reg4_5_p1} = maincontroller_1_ar__bus_inc_ld[2] ? {4'b0000, reg4_1_output} : 8'bz;  // Controlled_Buffer controlled_buffer_2
  assign {controlled_buffer_1_out, reg4_5_p1} = maincontroller_1_pc__bus_inc_ld[2] ? {4'b0000, reg4_2_output} : 8'bz;  // Controlled_Buffer controlled_buffer_3
  assign {controlled_buffer_1_out, reg4_5_p1} = maincontroller_1_ac_bus_clr_inc_ld[3] ? {4'b0000, reg4_4_output} : 8'bz;  // Controlled_Buffer controlled_buffer_4
  assign {controlled_buffer_1_out, reg4_5_p1} = maincontroller_1_ir_bus_ld[1] ? {4'b0000, reg8_1_ir} : 8'bz;  // Controlled_Buffer controlled_buffer_5

  // Notes on the sheet:
  //   AR
  //   DR
  //   PC
  //   AC
  //   OUTR
endmodule

module reg4 (
  input  INC,
  input  LD,
  input  [3:0] INPUT,
  input  CLR,
  input  CLK,
  output [3:0] OUTPUT
);

  wire and_1_out, and_2_out, and_3_out, and_4_out, and_5_out, and_6_out, and_7_out, and_8_out, and_9_out,
       and_10_out, and_11_out, and_12_out, not_1_out, not_2_out, not_3_out, not_4_out, not_5_out, not_6_out,
       or_1_out, or_2_out, or_3_out, or_4_out, or_5_out, or_6_out, or_7_out, or_8_out;

  and and_1 (and_1_out, INC, not_2_out);
  not not_1 (not_1_out, not_2_out);
  not not_2 (not_2_out, LD);
  not not_3 (not_3_out, INPUT[0]);
  not not_4 (not_4_out, INPUT[1]);
  not not_5 (not_5_out, INPUT[2]);
  not not_6 (not_6_out, INPUT[3]);
  and and_2 (and_2_out, not_1_out, INPUT[0]);
  and and_3 (and_3_out, not_1_out, not_3_out);
  and and_4 (and_4_out, not_1_out, INPUT[1]);
  and and_5 (and_5_out, not_1_out, not_4_out);
  and and_6 (and_6_out, not_1_out, INPUT[2]);
  and and_7 (and_7_out, not_1_out, not_5_out);
  and and_8 (and_8_out, not_1_out, INPUT[3]);
  and and_9 (and_9_out, not_1_out, not_6_out);
  and and_10 (and_10_out, and_1_out, OUTPUT[0]);
  and and_11 (and_11_out, and_1_out, OUTPUT[0], OUTPUT[1]);
  and and_12 (and_12_out, and_1_out, OUTPUT[0], OUTPUT[1], OUTPUT[2]);
  or or_1 (or_1_out, and_2_out, and_1_out);
  or or_2 (or_2_out, and_3_out, and_1_out);
  or or_3 (or_3_out, and_4_out, and_10_out);
  or or_4 (or_4_out, and_10_out, and_5_out);
  or or_5 (or_5_out, and_6_out, and_11_out);
  or or_6 (or_6_out, and_11_out, and_7_out);
  or or_7 (or_7_out, and_8_out, and_12_out);
  or or_8 (or_8_out, and_12_out, and_9_out);
  J_K_Flip_Flop j_k_ff_1 (.J(or_1_out), .clk(CLK), .K(or_2_out), .Q(OUTPUT[0]), .reset(CLR));  // open: Qn, preset, en
  J_K_Flip_Flop j_k_ff_2 (.J(or_3_out), .clk(CLK), .K(or_4_out), .Q(OUTPUT[1]), .reset(CLR));  // open: Qn, preset, en
  J_K_Flip_Flop j_k_ff_3 (.J(or_5_out), .clk(CLK), .K(or_6_out), .Q(OUTPUT[2]), .reset(CLR));  // open: Qn, preset, en
  J_K_Flip_Flop j_k_ff_4 (.J(or_7_out), .clk(CLK), .K(or_8_out), .Q(OUTPUT[3]), .reset(CLR));  // open: Qn, preset, en
endmodule

// IR
module reg8 (
  input  [7:0] INPUT,
  input  CLK,
  input  LD,
  output [3:0] IR,
  output [3:0] Decode_IR
);

  reg4 reg4_1 (.INPUT(INPUT[3:0]), .CLK(CLK), .LD(LD), .OUTPUT(IR));  // open: INC, CLR
  reg4 reg4_2 (.INPUT(INPUT[7:4]), .CLK(CLK), .LD(LD), .OUTPUT(Decode_IR));  // open: INC, CLR
endmodule

module ALU1 (
  input  INPR,
  input  DR,
  input  AC,
  input  cin,
  input  \and ,
  input  add,
  input  cma,
  input  ld_DR,
  input  ld_INPR,
  input  \cır ,
  input  cil,
  input  i_1,
  input  i_1_2,
  output \output ,
  output cout
);

  wire ADD_out, adder_1_out, and_1_out, AND_2_out, CIL_out, CIR_out, CMA_out, Ld_INPR_out, Ld_NPR_out,
       not_1_out;

  Adder #(.width(1)) adder_1 (.a(AC), .b(DR), .out(adder_1_out), .cin(cin), .cout(cout));
  and and_1 (and_1_out, AC, DR);
  not not_1 (not_1_out, AC);
  and AND_2 (AND_2_out, \and , and_1_out);
  and u_ADD (ADD_out, add, adder_1_out);
  and Ld_NPR (Ld_NPR_out, ld_DR, DR);
  and u_CMA (CMA_out, cma, not_1_out);
  and CIR (CIR_out, \cır , i_1_2);
  and u_CIL (CIL_out, cil, i_1);
  and u_Ld_INPR (Ld_INPR_out, ld_INPR, INPR);
  or or_1 (\output , AND_2_out, ADD_out, Ld_NPR_out, CMA_out, CIR_out, CIL_out, Ld_INPR_out);

  // Notes on the sheet:
  //   1 Bitlik ALU Devresi
endmodule

module ALU4 (
  input  [3:0] AC,
  input  [3:0] DR,
  input  [3:0] INPR,
  input  \and ,
  input  add,
  input  cma,
  input  LD_DR,
  input  LD_INPR,
  input  CIR,
  input  CIL,
  input  CLK,
  input  CLR,
  output [3:0] OUTPUT,
  output out_14
);

  wire alu1_1_cout, alu1_2_cout, alu1_3_cout, alu1_4_cout, e_1_ac_0__ac_i_1, e_1_ac_0__cin, e_1_ac_3__ac_i_1;

  ALU1 alu1_1 (
    .\and (\and ), .add(add), .cma(cma), .ld_DR(LD_DR), .ld_INPR(LD_INPR), .\cır (CIR), .cil(CIL),
    .i_1(e_1_ac_0__ac_i_1), .i_1_2(AC[1]), .INPR(INPR[0]), .DR(DR[0]), .AC(AC[0]), .cin(e_1_ac_0__cin),
    .cout(alu1_1_cout), .\output (OUTPUT[0]));
  ALU1 alu1_2 (
    .\and (\and ), .add(add), .cma(cma), .ld_DR(LD_DR), .ld_INPR(LD_INPR), .\cır (CIR), .cil(CIL),
    .i_1(AC[0]), .i_1_2(AC[2]), .INPR(INPR[1]), .DR(DR[1]), .AC(AC[1]), .cin(alu1_1_cout),
    .cout(alu1_2_cout), .\output (OUTPUT[1]));
  ALU1 alu1_3 (
    .\and (\and ), .add(add), .cma(cma), .ld_DR(LD_DR), .ld_INPR(LD_INPR), .\cır (CIR), .cil(CIL),
    .i_1(AC[1]), .i_1_2(AC[3]), .INPR(INPR[2]), .DR(DR[2]), .AC(AC[2]), .cin(alu1_2_cout),
    .cout(alu1_3_cout), .\output (OUTPUT[2]));
  ALU1 alu1_4 (
    .\and (\and ), .add(add), .cma(cma), .ld_DR(LD_DR), .ld_INPR(LD_INPR), .\cır (CIR), .cil(CIL),
    .i_1(AC[2]), .i_1_2(e_1_ac_3__ac_i_1), .INPR(INPR[3]), .DR(DR[3]), .AC(AC[3]), .cin(alu1_3_cout),
    .cout(alu1_4_cout), .\output (OUTPUT[3]));
  E e_1 (
    .AC_3__count(alu1_4_cout), .AC_3__output(AC[3]), .AC_0_output(AC[0]), .CIL(CIL), .CIR(CIR), .ADD(\and ),
    .CLK(CLK), .CLR(CLR), .output_E(out_14), .AC_0__ac_i_1(e_1_ac_0__ac_i_1),
    .AC_3__ac_i_1(e_1_ac_3__ac_i_1), .AC_0__cin(e_1_ac_0__cin));
endmodule

module E (
  input  AC_3__count,
  input  AC_3__output,
  input  AC_0_output,
  input  CIL,
  input  CIR,
  input  ADD,
  input  CLK,
  input  CLR,
  output output_E,
  output AC_0__ac_i_1,
  output AC_3__ac_i_1,
  output AC_0__cin
);

  wire and_1_out, and_2_out, and_3_out, and_4_out, and_5_out, d_ff_1_q, not_1_out, or_1_out, or_2_out;

  or or_1 (or_1_out, AC_3__count, AC_3__output, AC_0_output);
  and and_1 (and_1_out, AC_3__count, ADD);
  and and_2 (and_2_out, AC_0_output, CIR);
  and and_3 (and_3_out, AC_3__output, CIL);
  or or_2 (or_2_out, and_1_out, and_2_out, and_3_out);
  not not_1 (not_1_out, or_2_out);
  D_Flip_Flop d_ff_1 (.clk(CLK), .D(output_E), .Q(d_ff_1_q), .reset(CLR));  // open: Qn, preset, en
  and and_4 (and_4_out, or_2_out, or_1_out);
  J_K_Flip_Flop j_k_ff_1 (.J(and_4_out), .clk(CLK), .K(and_5_out), .Q(output_E), .reset(CLR));  // open: Qn, preset, en
  and and_5 (and_5_out, or_1_out, not_1_out);
  and and_6 (AC_0__ac_i_1, CIL, d_ff_1_q);
  and and_7 (AC_3__ac_i_1, CIR, d_ff_1_q);
  and and_8 (AC_0__cin, ADD, d_ff_1_q);
endmodule

module Bus (
  input  T0,
  input  T1,
  input  T2,
  input  T3,
  input  T4,
  input  D0,
  input  D1,
  input  D2,
  input  D3,
  input  D4,
  input  D5,
  input  D6,
  input  D14,
  output Memory_Bus,
  output AR_Bus,
  output DR_Bus,
  output AC_Bus,
  output PC_Bus,
  output IR_Bus
);

  wire and_1_out, and_2_out, and_3_out, and_4_out, and_5_out, and_6_out, or_1_out;

  or or_1 (or_1_out, D0, D1, D2, D6);
  and and_1 (and_1_out, T3, or_1_out);
  and and_2 (and_2_out, D4, T3);
  and and_3 (and_3_out, D5, T4);
  and and_4 (and_4_out, D3, T3);
  and and_5 (and_5_out, T3, D14);
  and and_6 (and_6_out, D5, T3);
  or M (Memory_Bus, T1, and_1_out);
  or AR (AR_Bus, and_2_out, and_3_out);
  and DR (DR_Bus, T4, D2);
  or AC (AC_Bus, and_4_out, and_5_out);
  or PC (PC_Bus, T0, and_6_out);

  assign IR_Bus = T2;
endmodule

// cont
module counter (
  input  CLK,
  input  SC_CLR,
  output [3:0] \output 
);

  wire and_1_out, register_1_q;

  Counter #(.width(4), .max('hf)) counter_1 (
    .count(1'b1), .Q(\output ), .clk(CLK), .clr(register_1_q));  // open: load, D, carry
  Register #(.width(1)) register_1 (.D(SC_CLR), .Q(register_1_q), .clk(CLK), .clr(and_1_out));  // open: en
  and and_1 (and_1_out, CLK, SC_CLR);
endmodule

// M[ ]
module Count_M (
  input  T1,
  input  T3,
  input  D0,
  input  D1,
  input  D2,
  input  D3,
  input  D5,
  input  D6,
  output M_LD,
  output M_BUS
);

  wire and_1_out, or_1_out, or_2_out;

  or or_1 (or_1_out, D0, D1, D2, D6);
  or or_2 (or_2_out, D3, D5);
  and and_1 (and_1_out, T3, or_1_out);
  and and_2 (M_LD, or_2_out, T3);
  or or_3 (M_BUS, T1, and_1_out);
endmodule

// AR
module Cont_AR (
  input  T0,
  input  T2,
  input  T3,
  input  T4,
  input  D4,
  input  D5,
  output AR_LD,
  output AR_INC,
  output AR_BUS
);

  wire and_1_out, and_2_out;

  and and_1 (and_1_out, D4, T3);
  and and_2 (and_2_out, D5, T4);
  or or_1 (AR_LD, T0, T2);
  and and_3 (AR_INC, D5, T3);
  or or_2 (AR_BUS, and_1_out, and_2_out);
endmodule

// PC
module Cont_PC (
  input  D4,
  input  D5,
  input  D6,
  input  T0,
  input  T1,
  input  T3,
  input  T4,
  output PC_LD,
  output PC_INC,
  output PC_BUS
);

  wire and_1_out, and_2_out, and_3_out, or_1_out;

  or or_1 (or_1_out, D4, D6);
  and and_1 (and_1_out, or_1_out, T3);
  and and_2 (and_2_out, D5, T4);
  and and_3 (and_3_out, D5, T3);
  or or_2 (PC_LD, and_1_out, and_2_out);
  or or_3 (PC_BUS, T0, and_3_out);

  assign PC_INC = T1;
endmodule

// DR
module Cont_DR (
  input  T3,
  input  D0,
  input  D1,
  input  D2,
  output DR_LD
);

  wire or_1_out;

  or or_1 (or_1_out, D2, D1, D0);
  and and_1 (DR_LD, T3, or_1_out);
endmodule

// IR
module Cont_IR (
  input  T1,
  input  T2,
  output IR_LD,
  output IR_BUS
);


  assign IR_BUS = T2;
  assign IR_LD = T1;
endmodule

// OutR
module Cont_OutR (
  input  T3,
  input  D14,
  output OutR_LD
);

  and and_1 (OutR_LD, D14, T3);
endmodule

// AC
module Count_Ac (
  input  T3,
  input  T4,
  input  D0,
  input  D1,
  input  D2,
  input  D3,
  input  D7,
  input  D9,
  input  D10,
  input  D11,
  input  D12,
  input  D13,
  input  D14,
  output AC_LD,
  output AC_INC,
  output AC_CLR,
  output AC_Bus
);

  wire and_1_out, and_2_out, or_1_out, or_2_out, or_3_out;

  or or_1 (or_1_out, D9, D11, D12, D13);
  or or_2 (or_2_out, D0, D1, D2);
  and and_1 (and_1_out, or_1_out, T3);
  and and_2 (and_2_out, or_2_out, T4);
  or or_3 (or_3_out, D3, D14);
  or or_4 (AC_LD, and_1_out, and_2_out);
  and and_3 (AC_INC, T3, D10);
  and and_4 (AC_CLR, T3, D7);
  and and_5 (AC_Bus, T3, or_3_out);
endmodule

module Cont_Alu (
  input  T3,
  input  T4,
  input  D0,
  input  D1,
  input  D2,
  input  D9,
  input  D11,
  input  D12,
  input  D13,
  output AND,
  output ADD,
  output CMA,
  output LD_DR,
  output LD_INPR,
  output CIR,
  output CIL
);

  and and_1 (AND, D0, T4);
  and and_2 (ADD, D1, T4);
  and and_3 (CMA, D9, T3);
  and and_4 (LD_DR, D2, T4);
  and and_5 (LD_INPR, D13, T3);
  and and_6 (CIR, D11, T3);
  and and_7 (CIL, D12, T3);
endmodule

module SC_CLR (
  input  T3,
  input  T4,
  input  D0,
  input  D1,
  input  D2,
  input  D3,
  input  D4,
  input  D5,
  input  D6,
  input  D7,
  input  D8,
  input  D9,
  input  D10,
  input  D11,
  input  D12,
  input  D13,
  input  D14,
  output SC_CLR
);

  wire and_1_out, and_2_out, or_1_out, or_2_out;

  or or_1 (or_1_out, D5, D2, D1, D0);
  or or_2 (or_2_out, D14, D13, D12, D11, D10, D9, D8, D7, D6, D4, D3);
  and and_1 (and_1_out, or_2_out, T3);
  and and_2 (and_2_out, or_1_out, T4);
  or or_3 (SC_CLR, and_1_out, and_2_out);
endmodule

module RegisterControl (
  input  T0,
  input  T1,
  input  T2,
  input  T3,
  input  T4,
  input  D0,
  input  D1,
  input  D2,
  input  D3,
  input  D4,
  input  D5,
  input  D6,
  input  D7,
  input  D8,
  input  D9,
  input  D10,
  input  D11,
  input  D12,
  input  D13,
  input  D14,
  output [1:0] M_____BUS_LD,
  output [2:0] AR__BUS_INC_LD,
  output [2:0] PC__BUS_INC_LD,
  output DR_LD,
  output [3:0] AC__BUS_CLR_INC_LD,
  output OUTR__LD,
  output [1:0] IR__BUS_LD
);

  Count_M count_m_1 (
    .T1(T1), .T3(T3), .D0(D0), .D1(D1), .D2(D2), .D3(D3), .D5(D5), .D6(D6), .M_LD(M_____BUS_LD[0]),
    .M_BUS(M_____BUS_LD[1]));
  Cont_AR cont_ar_1 (
    .T0(T0), .T2(T2), .T3(T3), .T4(T4), .D4(D4), .D5(D5), .AR_LD(AR__BUS_INC_LD[0]),
    .AR_INC(AR__BUS_INC_LD[1]), .AR_BUS(AR__BUS_INC_LD[2]));
  Cont_PC cont_pc_1 (
    .D4(T0), .D5(T1), .D6(T3), .T0(T4), .T1(D4), .T3(D5), .T4(D6), .PC_LD(PC__BUS_INC_LD[0]),
    .PC_INC(PC__BUS_INC_LD[1]), .PC_BUS(PC__BUS_INC_LD[2]));
  Cont_DR cont_dr_1 (.T3(T3), .D0(D0), .D1(D1), .D2(D2), .DR_LD(DR_LD));
  Cont_OutR cont_outr_1 (.T3(T3), .D14(D14), .OutR_LD(OUTR__LD));
  Cont_IR cont_ir_1 (.T1(T1), .T2(T2), .IR_LD(IR__BUS_LD[0]), .IR_BUS(IR__BUS_LD[1]));
  Count_Ac count_ac_1 (
    .T3(T3), .T4(T4), .D0(D0), .D1(D1), .D2(D2), .D3(D3), .D7(D7), .D9(D9), .D10(D10), .D11(D11), .D12(D12),
    .D13(D13), .D14(D14), .AC_LD(AC__BUS_CLR_INC_LD[0]), .AC_INC(AC__BUS_CLR_INC_LD[1]),
    .AC_CLR(AC__BUS_CLR_INC_LD[2]), .AC_Bus(AC__BUS_CLR_INC_LD[3]));

  // Notes on the sheet:
  //   M[ ]
  //   AR
  //   PC
  //   DR
  //   AC
  //   out
  //   IR
endmodule

// MainCont
module MainController (
  input  [3:0] IR_4__7,
  input  CLK,
  output [1:0] M_____BUS_LD,
  output [2:0] AR__BUS_INC_LD,
  output [2:0] PC__BUS_INC_LD,
  output DR_LD,
  output [3:0] AC_BUS_CLR_INC_LD,
  output Outr_LD,
  output [1:0] IR_BUS_LD,
  output [6:0] ALU,
  output HLT,
  output E_CLR
);

  wire decoder_1_out15, sc_clr_1_sc_clr;
  wire [1:0] decoder_2_out1;
  wire [3:0] counter_1_output, decoder_2_out2;
  wire [14:0] decoder_1_out4;

  SC_CLR sc_clr_1 (
    .T3(decoder_2_out1[1]), .T4(decoder_2_out2[3]), .D0(decoder_1_out4[0]), .D1(decoder_1_out4[1]),
    .D2(decoder_1_out4[2]), .D3(decoder_1_out4[3]), .D4(decoder_1_out4[4]), .D5(decoder_1_out4[5]),
    .D6(decoder_1_out4[6]), .D7(decoder_1_out4[7]), .D8(decoder_1_out4[8]), .D9(decoder_1_out4[9]),
    .D10(decoder_1_out4[10]), .D11(decoder_1_out4[11]), .D12(decoder_1_out4[12]), .D13(decoder_1_out4[13]),
    .D14(decoder_1_out4[14]), .SC_CLR(sc_clr_1_sc_clr));
  counter counter_1 (.CLK(CLK), .SC_CLR(sc_clr_1_sc_clr), .\output (counter_1_output));
  Decoder #(.select(4)) decoder_1 (
    .out0(decoder_1_out4[0]), .out1(decoder_1_out4[1]), .out2(decoder_1_out4[2]), .out3(decoder_1_out4[3]),
    .out4(decoder_1_out4[4]), .out5(decoder_1_out4[5]), .out6(decoder_1_out4[6]), .out7(decoder_1_out4[7]),
    .out8(decoder_1_out4[8]), .out9(decoder_1_out4[9]), .out10(decoder_1_out4[10]),
    .out11(decoder_1_out4[11]), .out12(decoder_1_out4[12]), .out13(decoder_1_out4[13]),
    .out14(decoder_1_out4[14]), .out15(decoder_1_out15), .sel(IR_4__7));  // open: en
  Decoder #(.select(4)) decoder_2 (
    .out0(decoder_2_out2[0]), .out1(decoder_2_out1[0]), .out2(decoder_2_out2[1]), .out3(decoder_2_out1[1]),
    .out4(decoder_2_out2[3]), .sel(counter_1_output));  // open: out5, out6, out7, out8, out9, out10, out11, out12, out13, out14, out15, en
  and and_1 (HLT, decoder_1_out15, decoder_2_out1[1]);
  and and_2 (E_CLR, decoder_1_out4[8], decoder_2_out1[1]);
  Cont_AR cont_ar_1 (
    .T0(decoder_2_out2[0]), .T2(decoder_2_out2[1]), .T3(decoder_2_out1[1]), .T4(decoder_2_out2[3]),
    .D4(decoder_1_out4[5]), .D5(decoder_1_out4[4]), .AR_LD(AR__BUS_INC_LD[0]), .AR_INC(AR__BUS_INC_LD[1]),
    .AR_BUS(AR__BUS_INC_LD[2]));
  Cont_PC cont_pc_1 (
    .D4(decoder_1_out4[4]), .D5(decoder_1_out4[5]), .D6(decoder_1_out4[6]), .T0(decoder_2_out2[0]),
    .T1(decoder_2_out1[0]), .T3(decoder_2_out1[1]), .T4(decoder_2_out2[3]), .PC_LD(PC__BUS_INC_LD[0]),
    .PC_INC(PC__BUS_INC_LD[1]), .PC_BUS(PC__BUS_INC_LD[2]));
  Cont_DR cont_dr_1 (
    .T3(decoder_2_out1[1]), .D0(decoder_1_out4[0]), .D1(decoder_1_out4[1]), .D2(decoder_1_out4[2]),
    .DR_LD(DR_LD));
  Cont_IR cont_ir_1 (.T1(decoder_2_out1[0]), .T2(decoder_2_out2[1]), .IR_LD(IR_BUS_LD[0]), .IR_BUS(IR_BUS_LD[1]));
  Cont_OutR cont_outr_1 (.T3(decoder_2_out1[1]), .D14(decoder_1_out4[14]), .OutR_LD(Outr_LD));
  Count_M count_m_1 (
    .T1(decoder_2_out1[0]), .T3(decoder_2_out1[1]), .D0(decoder_1_out4[0]), .D1(decoder_1_out4[1]),
    .D2(decoder_1_out4[2]), .D3(decoder_1_out4[3]), .D5(decoder_1_out4[5]), .D6(decoder_1_out4[6]),
    .M_LD(M_____BUS_LD[0]), .M_BUS(M_____BUS_LD[1]));
  Count_Ac count_ac_1 (
    .T3(decoder_2_out1[1]), .T4(decoder_2_out2[3]), .D0(decoder_1_out4[0]), .D1(decoder_1_out4[1]),
    .D2(decoder_1_out4[2]), .D3(decoder_1_out4[3]), .D7(decoder_1_out4[7]), .D9(decoder_1_out4[9]),
    .D10(decoder_1_out4[10]), .D11(decoder_1_out4[11]), .D12(decoder_1_out4[12]), .D13(decoder_1_out4[13]),
    .D14(decoder_1_out4[14]), .AC_LD(AC_BUS_CLR_INC_LD[0]), .AC_INC(AC_BUS_CLR_INC_LD[1]),
    .AC_CLR(AC_BUS_CLR_INC_LD[2]), .AC_Bus(AC_BUS_CLR_INC_LD[3]));
  Cont_Alu cont_alu_1 (
    .T3(decoder_2_out1[1]), .T4(decoder_2_out2[3]), .D0(decoder_1_out4[0]), .D1(decoder_1_out4[1]),
    .D2(decoder_1_out4[2]), .D9(decoder_1_out4[9]), .D11(decoder_1_out4[11]), .D12(decoder_1_out4[12]),
    .D13(decoder_1_out4[13]), .AND(ALU[0]), .ADD(ALU[1]), .CMA(ALU[2]), .LD_DR(ALU[3]), .LD_INPR(ALU[4]),
    .CIR(ALU[5]), .CIL(ALU[6]));

  // Notes on the sheet:
  //   D(0..14)
  //   D(0..15)
  //   T(0..4)
endmodule
